# Fritzing sketch particle1 (saved by Fritzing 0.9.2b)
breadboards: 1

parts:
  Part1 = Photon
  transistor1 = NPN-Transistor [package="TO92 [THT]"]
  jawServo = Basic Servo
  neckTiltServo = Basic Servo
  neckPanServo = Basic Servo
  transistor2 = NPN-Transistor [package="SOT-23 [SMD]"]
  led1 = LEDs [package=led10mm]
  led2 = LEDs [package=led10mm]
  R1_(1K) = Resistor [tolerance=±5% resistance=220 package=THT]
  R2_(1K) = Resistor [tolerance=±5% resistance=220 package=THT]
  PIR1 = PIR sensor
  R2 = Resistor [tolerance=±5% resistance=220 package=THT]
  R3 = Resistor [tolerance=±5% resistance=220 package=THT]
  BAT_6V = Battery Holders [package=lipo-1100mAh]
  BAT_5V = Battery Holders [package=lipo-1100mAh]

nets:
  GND: Part1.GND, transistor1.E, jawServo.gnd, neckTiltServo.gnd, neckPanServo.gnd, transistor2.2, led1.C, led2.C, PIR1.GND, BAT_6V.-, BAT_5V.-
  VIN: Part1.VIN, PIR1.VDD
  N1: Part1.D0, jawServo.pulse
  N2: Part1.D1, neckPanServo.pulse
  N3: Part1.D2, neckTiltServo.pulse
  N4: Part1.D3, R2.Pin_0
  N5: Part1.D4, R2_(1K).Pin_0
  N6: Part1.D5, R1_(1K).Pin_0
  N7: Part1.D6, R3.Pin_0
  N8: Part1.D7, PIR1.SIG
  N9: Part1.VBAT, BAT_5V.+
  N10: transistor1.B, R2_(1K).Pin_1
  VCC: jawServo.vcc, neckTiltServo.vcc, neckPanServo.vcc, BAT_6V.+
  N11: transistor2.0, R1_(1K).Pin_1
  N12: led1.A, R2.Pin_1
  N13: led2.A, R3.Pin_1
